# Fritzing sketch circuito_rasp (saved by Fritzing 0.9.3b)

parts:
  MCU1 = Raspberry Pi Zero
  KY-1 = Keyes Relay [package=THT]
  VCC1 = Battery
  U1 = GPS-09838 [package=ls20126]  # not connected
  USBTTL2 = Micro USB B Plug  # not connected
  SPKR1 = Loudspeaker
  M1 = RioRand LM2596

nets:
  N1: MCU1.pin_4, M1.Pin_3
  N2: MCU1.pin_6, MCU1.pin_9, MCU1.pin_34, KY-1.ground, M1.Pin_4
  N3: MCU1.pin_8, KY-1.signal
  N4: KY-1.C, VCC1.+, M1.Pin_1
  N5: KY-1.NO, SPKR1.pin2
  N6: VCC1.-, SPKR1.pin1, M1.Pin_2

custom parts:
  Keyes Relay: The Keyes 5V relay module is suitable for SCM development, home appliance control. It uses a 5V~12V TIL control signal which can control DC / AC signal.
